// Logisim project JOGO DA MEMÓRIA.circ as structural Verilog: 1 circuit, main circuit main
module main (
);

  wire ACERTO_00, ACERTO_01, ACERTO_02, ACERTO_03, ACERTO_10, ACERTO_11, ACERTO_12, ACERTO_13, ACERTO_20,
       ACERTO_21, ACERTO_22, ACERTO_23, ACERTO_30, ACERTO_31, ACERTO_32, ACERTO_33, and_17_out, and_18_out,
       and_19_out, and_20_out, and_21_out, and_22_out, and_23_out, and_24_out, and_25_out, and_26_out,
       and_27_out, and_28_out, and_30_out, and_31_out, and_40_out, and_41_out, and_42_out, and_43_out,
       and_44_out, and_45_out, and_46_out, and_47_out, and_48_out, and_49_out, and_50_out, and_51_out,
       and_52_out, and_53_out, and_54_out, and_55_out, and_56_out, and_57_out, and_58_out, and_59_out,
       and_60_out, and_61_out, and_62_out, and_63_out, and_64_out, and_65_out, and_66_out, and_67_out,
       and_68_out, and_69_out, and_74_out, and_75_out, and_76_out, and_77_out, and_78_out, and_79_out,
       and_80_out, and_81_out, and_82_out, and_83_out, and_84_out, and_85_out, and_90_out, and_91_out,
       and_92_out, and_93_out, and_94_out, and_95_out, and_96_out, and_97_out, and_98_out, and_99_out,
       and_100_out, and_101_out, COLUNA, CONDICIONAL, CONFIRMA, demultiplexer_1_out0, demultiplexer_1_out1,
       demultiplexer_1_out2, demultiplexer_1_out3, demultiplexer_2_out0, demultiplexer_2_out1,
       demultiplexer_2_out2, demultiplexer_2_out3, ESTADO_00, ESTADO_01, ESTADO_02, ESTADO_03, IGUAIS, L00,
       L01, L02, L03, L10, L11, L12, L13, L20, L21, L22, L23, L30, L31, L32, L33, LINHA, OP_VALIDA, or_1_out,
       or_2_out, or_3_out, or_4_out, or_5_out, or_6_out, or_7_out, or_8_out, or_9_out, or_10_out, or_11_out,
       or_12_out, or_13_out, or_14_out, or_15_out, or_16_out, or_17_out, or_19_out, or_20_out, or_21_out,
       or_22_out, or_23_out, or_24_out, or_25_out, or_26_out, or_27_out, or_28_out, or_29_out, or_30_out,
       or_31_out, or_32_out, or_33_out, or_34_out, RESET, RET_P00, RET_P01, RET_P02, RET_P03, RET_P10,
       RET_P11, RET_P12, RET_P13, RET_P20, RET_P21, RET_P22, RET_P23, RET_P30, RET_P31, RET_P32, RET_P33,
       VEZ_01, VEZ_02;
  wire [1:0] COLUNA_01, COLUNA_02, COLUNA_P, counter_4_q, LINHA_01, LINHA_02, LINHA_P;
  wire [3:0] multiplexer_1_out, multiplexer_2_out, P00, P01, P02, P03, P10, P11, P12, P13, P20, P21, P22,
       P23, P30, P31, P32, P33, PLAYER_01, PLAYER_02;

  LED led_1 (.in(VEZ_01));
  Hex_Digit_Display hex_digit_display_1 (.value(PLAYER_01));  // open: dp
  Counter #(.width(2), .max('h3)) counter_1 (.Q(COLUNA_P), .clk(COLUNA), .clr(RESET));  // open: load, D, count, carry
  Counter #(.width(2), .max('h3)) counter_2 (.Q(LINHA_P), .clk(LINHA), .clr(RESET));  // open: load, D, count, carry
  Button button_1 (.out(LINHA));
  Button button_2 (.out(COLUNA));
  Button button_3 (.out(CONFIRMA));
  Button button_4 (.out(RESET));
  Demultiplexer #(.select(2), .tristate("true"), .disabled(0), .enable("false")) demultiplexer_1 (
    .out0(demultiplexer_1_out0), .out1(demultiplexer_1_out1), .out2(demultiplexer_1_out2),
    .out3(demultiplexer_1_out3), .in(1'b1), .sel(LINHA_P));
  LED led_2 (.in(VEZ_02));
  Hex_Digit_Display hex_digit_display_2 (.value(PLAYER_02));  // open: dp
  Demultiplexer #(.select(2), .tristate("true"), .disabled(0), .enable("false")) demultiplexer_2 (
    .out0(demultiplexer_2_out0), .out1(demultiplexer_2_out1), .out2(demultiplexer_2_out2),
    .out3(demultiplexer_2_out3), .in(1'b1), .sel(COLUNA_P));
  Multiplexer #(.select(4), .width(4), .enable("false")) multiplexer_1 (
    .in0(4'b1001), .in1(4'b1000), .in2(4'b0111), .in3(4'b0101), .in4(4'b0010), .in5(4'b0100), .in6(4'b0101),
    .in7(4'b0010), .in8(4'b0110), .in9(4'b1000), .in10(4'b1001), .in11(4'b0100), .in12(4'b0011),
    .in13(4'b0110), .in14(4'b0011), .in15(4'b0111), .out(multiplexer_1_out), .sel({LINHA_01, COLUNA_01}));
  Multiplexer #(.select(4), .width(4), .enable("false")) multiplexer_2 (
    .in0(4'b1001), .in1(4'b1000), .in2(4'b0111), .in3(4'b0101), .in4(4'b0010), .in5(4'b0100), .in6(4'b0101),
    .in7(4'b0010), .in8(4'b0110), .in9(4'b1000), .in10(4'b1001), .in11(4'b0100), .in12(4'b0011),
    .in13(4'b0110), .in14(4'b0011), .in15(4'b0111), .out(multiplexer_2_out), .sel({LINHA_02, COLUNA_02}));
  and and_1 (L00, demultiplexer_1_out0, demultiplexer_2_out0);
  and and_2 (L01, demultiplexer_1_out0, demultiplexer_2_out1);
  and and_3 (L02, demultiplexer_1_out0, demultiplexer_2_out2);
  and and_4 (L03, demultiplexer_1_out0, demultiplexer_2_out3);
  and and_5 (L10, demultiplexer_1_out1, demultiplexer_2_out0);
  and and_6 (L11, demultiplexer_1_out1, demultiplexer_2_out1);
  and and_7 (L12, demultiplexer_1_out1, demultiplexer_2_out2);
  and and_8 (L13, demultiplexer_1_out1, demultiplexer_2_out3);
  and and_9 (L20, demultiplexer_1_out2, demultiplexer_2_out0);
  and and_10 (L21, demultiplexer_1_out2, demultiplexer_2_out1);
  and and_11 (L22, demultiplexer_1_out2, demultiplexer_2_out2);
  and and_12 (L23, demultiplexer_1_out2, demultiplexer_2_out3);
  and and_13 (L30, demultiplexer_1_out3, demultiplexer_2_out0);
  and and_14 (L31, demultiplexer_1_out3, demultiplexer_2_out1);
  and and_15 (L32, demultiplexer_1_out3, demultiplexer_2_out2);
  and and_16 (L33, demultiplexer_1_out3, demultiplexer_2_out3);
  Hex_Digit_Display hex_digit_display_3 (.value(multiplexer_1_out));  // open: dp
  Hex_Digit_Display hex_digit_display_4 (.value(multiplexer_2_out));  // open: dp
  LED led_3 (.in(L00));
  Hex_Digit_Display hex_digit_display_5 (.value(P00));  // open: dp
  LED led_4 (.in(L10));
  Hex_Digit_Display hex_digit_display_6 (.value(P10));  // open: dp
  LED led_5 (.in(L20));
  Hex_Digit_Display hex_digit_display_7 (.value(P20));  // open: dp
  LED led_6 (.in(L30));
  Hex_Digit_Display hex_digit_display_8 (.value(P30));  // open: dp
  and and_17 (and_17_out, ~ESTADO_00, ~LINHA_01[0], ~LINHA_01[1], ~COLUNA_01[0], ~COLUNA_01[1]);  // AND_Gate
  and and_18 (and_18_out, ESTADO_02, ~LINHA_02[0], ~LINHA_02[1], ~COLUNA_02[0], ~COLUNA_02[1]);  // AND_Gate
  or or_1 (or_1_out, and_18_out, and_17_out);
  Comparator #(.width(4)) comparator_1 (
    .a(multiplexer_1_out), .b(multiplexer_2_out), .eq(CONDICIONAL));  // open: gt, lt
  and and_19 (and_19_out, or_1_out, IGUAIS, ESTADO_03, ~RET_P00);  // AND_Gate
  and and_20 (and_20_out, ~ESTADO_00, LINHA_01[0], ~LINHA_01[1], ~COLUNA_01[0], ~COLUNA_01[1]);  // AND_Gate
  and and_21 (and_21_out, ESTADO_02, LINHA_02[0], ~LINHA_02[1], ~COLUNA_02[0], ~COLUNA_02[1]);  // AND_Gate
  or or_2 (or_2_out, and_21_out, and_20_out);
  and and_22 (and_22_out, ~ESTADO_00, ~LINHA_01[0], LINHA_01[1], ~COLUNA_01[0], ~COLUNA_01[1]);  // AND_Gate
  and and_23 (and_23_out, ESTADO_02, ~LINHA_02[0], LINHA_02[1], ~COLUNA_02[0], ~COLUNA_02[1]);  // AND_Gate
  or or_3 (or_3_out, and_23_out, and_22_out);
  and and_24 (and_24_out, ~ESTADO_00, LINHA_01[0], LINHA_01[1], ~COLUNA_01[0], ~COLUNA_01[1]);  // AND_Gate
  and and_25 (and_25_out, ESTADO_02, LINHA_02[0], LINHA_02[1], ~COLUNA_02[0], ~COLUNA_02[1]);  // AND_Gate
  or or_4 (or_4_out, and_25_out, and_24_out);
  LED led_7 (.in(L01));
  Hex_Digit_Display hex_digit_display_9 (.value(P01));  // open: dp
  LED led_8 (.in(L11));
  Hex_Digit_Display hex_digit_display_10 (.value(P11));  // open: dp
  LED led_9 (.in(L21));
  Hex_Digit_Display hex_digit_display_11 (.value(P21));  // open: dp
  LED led_10 (.in(L31));
  Hex_Digit_Display hex_digit_display_12 (.value(P31));  // open: dp
  Counter #(.width(1), .max('h1)) counter_3 (
    .Q(RET_P00), .clk(and_19_out), .clr(RESET));  // open: load, D, count, carry
  and and_26 (and_26_out, or_2_out, IGUAIS, ESTADO_03, ~RET_P10);  // AND_Gate
  and and_27 (and_27_out, or_3_out, IGUAIS, ESTADO_03, ~RET_P20);  // AND_Gate
  and and_28 (and_28_out, or_4_out, IGUAIS, ESTADO_03, ~RET_P30);  // AND_Gate
  LED led_11 (.in(L02));
  Hex_Digit_Display hex_digit_display_13 (.value(P02));  // open: dp
  LED led_12 (.in(L12));
  Hex_Digit_Display hex_digit_display_14 (.value(P12));  // open: dp
  LED led_13 (.in(L22));
  Hex_Digit_Display hex_digit_display_15 (.value(P22));  // open: dp
  LED led_14 (.in(L32));
  Hex_Digit_Display hex_digit_display_16 (.value(P32));  // open: dp
  Counter #(.width(2), .max('h3)) counter_4 (
    .Q(counter_4_q), .clk(CONFIRMA), .clr(or_5_out));  // open: load, D, count, carry
  or or_5 (or_5_out, ESTADO_03, RESET);
  Counter #(.width(1), .max('h1), .trigger("falling")) counter_5 (
    .Q(VEZ_02), .clk(ESTADO_03), .clr(RESET));  // open: load, D, count, carry
  or or_6 (or_6_out, and_17_out, and_18_out, RET_P00);
  and and_29 (ACERTO_00, ~RET_P00, or_1_out);  // AND_Gate
  Counter #(.width(1), .max('h1)) counter_6 (
    .Q(RET_P10), .clk(and_26_out), .clr(RESET));  // open: load, D, count, carry
  Counter #(.width(1), .max('h1)) counter_7 (
    .Q(RET_P20), .clk(and_27_out), .clr(RESET));  // open: load, D, count, carry
  Counter #(.width(1), .max('h1)) counter_8 (
    .Q(RET_P30), .clk(and_28_out), .clr(RESET));  // open: load, D, count, carry
  LED led_15 (.in(L03));
  Hex_Digit_Display hex_digit_display_17 (.value(P03));  // open: dp
  LED led_16 (.in(L13));
  Hex_Digit_Display hex_digit_display_18 (.value(P13));  // open: dp
  LED led_17 (.in(L23));
  Hex_Digit_Display hex_digit_display_19 (.value(P23));  // open: dp
  LED led_18 (.in(L33));
  Hex_Digit_Display hex_digit_display_20 (.value(P33));  // open: dp
  and and_30 (and_30_out, ESTADO_00, CONFIRMA);
  and and_31 (and_31_out, ESTADO_01, CONFIRMA);
  not not_1 (VEZ_01, VEZ_02);
  and and_32 (IGUAIS, OP_VALIDA, CONDICIONAL, ESTADO_03);
  Multiplexer #(.width(4)) multiplexer_3 (.in1(4'b1001), .out(P00), .sel(or_6_out));  // open: in0, en
  or or_7 (or_7_out, and_20_out, and_21_out, RET_P10);
  and and_33 (ACERTO_10, ~RET_P10, or_2_out);  // AND_Gate
  or or_8 (or_8_out, and_22_out, and_23_out, RET_P20);
  and and_34 (ACERTO_20, ~RET_P20, or_3_out);  // AND_Gate
  or or_9 (or_9_out, and_24_out, and_25_out, RET_P30);
  and and_35 (ACERTO_30, ~RET_P30, or_4_out);  // AND_Gate
  Register #(.width(2)) register_1 (.D(LINHA_P), .Q(LINHA_01), .clk(and_30_out), .clr(RESET));  // open: en
  Register #(.width(2)) register_2 (.D(LINHA_P), .Q(LINHA_02), .clk(and_31_out), .clr(RESET));  // open: en
  Multiplexer #(.width(4)) multiplexer_4 (.in1(4'b0010), .out(P10), .sel(or_7_out));  // open: in0, en
  Multiplexer #(.width(4)) multiplexer_5 (.in1(4'b0110), .out(P20), .sel(or_8_out));  // open: in0, en
  Multiplexer #(.width(4)) multiplexer_6 (.in1(4'b0011), .out(P30), .sel(or_9_out));  // open: in0, en
  and and_36 (ESTADO_00, ~counter_4_q[0], ~counter_4_q[1]);  // AND_Gate
  and and_37 (ESTADO_01, counter_4_q[0], ~counter_4_q[1]);  // AND_Gate
  and and_38 (ESTADO_02, ~counter_4_q[0], counter_4_q[1]);  // AND_Gate
  and and_39 (ESTADO_03, counter_4_q[0], counter_4_q[1]);
  and and_40 (and_40_out, IGUAIS, VEZ_01);
  and and_41 (and_41_out, VEZ_02, IGUAIS);
  Counter #(.width(4), .max('hf)) counter_9 (
    .Q(PLAYER_01), .clk(and_40_out), .clr(RESET));  // open: load, D, count, carry
  Counter #(.width(4), .max('hf)) counter_10 (
    .Q(PLAYER_02), .clk(and_41_out), .clr(RESET));  // open: load, D, count, carry
  Register #(.width(2)) register_3 (.D(COLUNA_P), .Q(COLUNA_01), .clk(and_30_out), .clr(RESET));  // open: en
  Register #(.width(2)) register_4 (.D(COLUNA_P), .Q(COLUNA_02), .clk(and_31_out), .clr(RESET));  // open: en
  and and_42 (and_42_out, ACERTO_00, ACERTO_22);
  and and_43 (and_43_out, ACERTO_01, ACERTO_21);
  and and_44 (and_44_out, ACERTO_02, ACERTO_33);
  and and_45 (and_45_out, ACERTO_03, ACERTO_12);
  and and_46 (and_46_out, ACERTO_10, ACERTO_13);
  and and_47 (and_47_out, ACERTO_23, ACERTO_11);
  and and_48 (and_48_out, ACERTO_20, ACERTO_31);
  and and_49 (and_49_out, ACERTO_32, ACERTO_30);
  and and_50 (and_50_out, ~ESTADO_00, ~LINHA_01[0], ~LINHA_01[1], COLUNA_01[0], ~COLUNA_01[1]);  // AND_Gate
  and and_51 (and_51_out, ESTADO_02, ~LINHA_02[0], ~LINHA_02[1], COLUNA_02[0], ~COLUNA_02[1]);  // AND_Gate
  or or_10 (or_10_out, and_51_out, and_50_out);
  and and_52 (and_52_out, ~ESTADO_00, LINHA_01[0], ~LINHA_01[1], COLUNA_01[0], ~COLUNA_01[1]);  // AND_Gate
  and and_53 (and_53_out, ESTADO_02, LINHA_02[0], ~LINHA_02[1], COLUNA_02[0], ~COLUNA_02[1]);  // AND_Gate
  or or_11 (or_11_out, and_53_out, and_52_out);
  and and_54 (and_54_out, ~ESTADO_00, ~LINHA_01[0], LINHA_01[1], COLUNA_01[0], ~COLUNA_01[1]);  // AND_Gate
  and and_55 (and_55_out, ESTADO_02, ~LINHA_02[0], LINHA_02[1], COLUNA_02[0], ~COLUNA_02[1]);  // AND_Gate
  or or_12 (or_12_out, and_55_out, and_54_out);
  and and_56 (and_56_out, ~ESTADO_00, LINHA_01[0], LINHA_01[1], COLUNA_01[0], ~COLUNA_01[1]);  // AND_Gate
  and and_57 (and_57_out, ESTADO_02, LINHA_02[0], LINHA_02[1], COLUNA_02[0], ~COLUNA_02[1]);  // AND_Gate
  or or_13 (or_13_out, and_57_out, and_56_out);
  and and_58 (and_58_out, or_10_out, IGUAIS, ESTADO_03, ~RET_P01);  // AND_Gate
  and and_59 (and_59_out, or_11_out, IGUAIS, ESTADO_03, ~RET_P11);  // AND_Gate
  and and_60 (and_60_out, or_12_out, IGUAIS, ESTADO_03, ~RET_P21);  // AND_Gate
  and and_61 (and_61_out, or_13_out, IGUAIS, ESTADO_03, ~RET_P31);  // AND_Gate
  and and_62 (and_62_out, CONDICIONAL, and_42_out);
  and and_63 (and_63_out, CONDICIONAL, and_43_out);
  and and_64 (and_64_out, CONDICIONAL, and_44_out);
  and and_65 (and_65_out, CONDICIONAL, and_45_out);
  and and_66 (and_66_out, CONDICIONAL, and_46_out);
  and and_67 (and_67_out, CONDICIONAL, and_47_out);
  and and_68 (and_68_out, CONDICIONAL, and_48_out);
  and and_69 (and_69_out, CONDICIONAL, and_49_out);
  Counter #(.width(1), .max('h1)) counter_11 (
    .Q(RET_P01), .clk(and_58_out), .clr(RESET));  // open: load, D, count, carry
  Counter #(.width(1), .max('h1)) counter_12 (
    .Q(RET_P11), .clk(and_59_out), .clr(RESET));  // open: load, D, count, carry
  Counter #(.width(1), .max('h1)) counter_13 (
    .Q(RET_P21), .clk(and_60_out), .clr(RESET));  // open: load, D, count, carry
  Counter #(.width(1), .max('h1)) counter_14 (
    .Q(RET_P31), .clk(and_61_out), .clr(RESET));  // open: load, D, count, carry
  Multiplexer #(.width(4)) multiplexer_7 (.in1(4'b1000), .out(P01), .sel(or_14_out));  // open: in0, en
  or or_14 (or_14_out, and_50_out, and_51_out, RET_P01);
  and and_70 (ACERTO_01, ~RET_P01, or_10_out);  // AND_Gate
  or or_15 (or_15_out, and_52_out, and_53_out, RET_P11);
  and and_71 (ACERTO_11, ~RET_P11, or_11_out);  // AND_Gate
  or or_16 (or_16_out, and_54_out, and_55_out, RET_P21);
  and and_72 (ACERTO_21, ~RET_P21, or_12_out);  // AND_Gate
  or or_17 (or_17_out, and_56_out, and_57_out, RET_P31);
  and and_73 (ACERTO_31, ~RET_P31, or_13_out);  // AND_Gate
  or or_18 (OP_VALIDA, and_62_out, and_63_out, and_64_out, and_65_out, and_66_out, and_67_out, and_68_out, and_69_out);
  Multiplexer #(.width(4)) multiplexer_8 (.in1(4'b0100), .out(P11), .sel(or_15_out));  // open: in0, en
  Multiplexer #(.width(4)) multiplexer_9 (.in1(4'b1000), .out(P21), .sel(or_16_out));  // open: in0, en
  Multiplexer #(.width(4)) multiplexer_10 (.in1(4'b0110), .out(P31), .sel(or_17_out));  // open: in0, en
  and and_74 (and_74_out, ~ESTADO_00, ~LINHA_01[0], ~LINHA_01[1], ~COLUNA_01[0], COLUNA_01[1]);  // AND_Gate
  and and_75 (and_75_out, ESTADO_02, ~LINHA_02[0], ~LINHA_02[1], ~COLUNA_02[0], COLUNA_02[1]);  // AND_Gate
  or or_19 (or_19_out, and_75_out, and_74_out);
  and and_76 (and_76_out, ~ESTADO_00, LINHA_01[0], ~LINHA_01[1], ~COLUNA_01[0], COLUNA_01[1]);  // AND_Gate
  and and_77 (and_77_out, ESTADO_02, LINHA_02[0], ~LINHA_02[1], ~COLUNA_02[0], COLUNA_02[1]);  // AND_Gate
  or or_20 (or_20_out, and_77_out, and_76_out);
  and and_78 (and_78_out, ~ESTADO_00, ~LINHA_01[0], LINHA_01[1], ~COLUNA_01[0], COLUNA_01[1]);  // AND_Gate
  and and_79 (and_79_out, ESTADO_02, ~LINHA_02[0], LINHA_02[1], ~COLUNA_02[0], COLUNA_02[1]);  // AND_Gate
  or or_21 (or_21_out, and_79_out, and_78_out);
  and and_80 (and_80_out, ~ESTADO_00, LINHA_01[0], LINHA_01[1], ~COLUNA_01[0], COLUNA_01[1]);  // AND_Gate
  and and_81 (and_81_out, ESTADO_02, LINHA_02[0], LINHA_02[1], ~COLUNA_02[0], COLUNA_02[1]);  // AND_Gate
  or or_22 (or_22_out, and_81_out, and_80_out);
  Counter #(.width(1), .max('h1)) counter_15 (
    .Q(RET_P02), .clk(and_82_out), .clr(RESET));  // open: load, D, count, carry
  and and_82 (and_82_out, or_19_out, IGUAIS, ESTADO_03, ~RET_P02);  // AND_Gate
  and and_83 (and_83_out, or_20_out, IGUAIS, ESTADO_03, ~RET_P12);  // AND_Gate
  Counter #(.width(1), .max('h1)) counter_16 (
    .Q(RET_P22), .clk(and_84_out), .clr(RESET));  // open: load, D, count, carry
  and and_84 (and_84_out, or_21_out, IGUAIS, ESTADO_03, ~RET_P22);  // AND_Gate
  and and_85 (and_85_out, or_22_out, IGUAIS, ESTADO_03, ~RET_P32);  // AND_Gate
  or or_23 (or_23_out, and_74_out, and_75_out, RET_P02);
  Counter #(.width(1), .max('h1)) counter_17 (
    .Q(RET_P12), .clk(and_83_out), .clr(RESET));  // open: load, D, count, carry
  and and_86 (ACERTO_22, ~RET_P22, or_21_out);  // AND_Gate
  Counter #(.width(1), .max('h1)) counter_18 (
    .Q(RET_P32), .clk(and_85_out), .clr(RESET));  // open: load, D, count, carry
  Multiplexer #(.width(4)) multiplexer_11 (.in1(4'b0111), .out(P02), .sel(or_23_out));  // open: in0, en
  and and_87 (ACERTO_02, ~RET_P02, or_19_out);  // AND_Gate
  Multiplexer #(.width(4)) multiplexer_12 (.in1(4'b0101), .out(P12), .sel(or_24_out));  // open: in0, en
  or or_24 (or_24_out, and_76_out, and_77_out, RET_P12);
  and and_88 (ACERTO_12, ~RET_P12, or_20_out);  // AND_Gate
  Multiplexer #(.width(4)) multiplexer_13 (.in1(4'b1001), .out(P22), .sel(or_25_out));  // open: in0, en
  or or_25 (or_25_out, and_78_out, and_79_out, RET_P22);
  or or_26 (or_26_out, and_80_out, and_81_out, RET_P32);
  and and_89 (ACERTO_32, ~RET_P32, or_22_out);  // AND_Gate
  Multiplexer #(.width(4)) multiplexer_14 (.in1(4'b0011), .out(P32), .sel(or_26_out));  // open: in0, en
  and and_90 (and_90_out, ~ESTADO_00, ~LINHA_01[0], ~LINHA_01[1], COLUNA_01[0], COLUNA_01[1]);  // AND_Gate
  and and_91 (and_91_out, ESTADO_02, ~LINHA_02[0], ~LINHA_02[1], COLUNA_02[0], COLUNA_02[1]);  // AND_Gate
  or or_27 (or_27_out, and_91_out, and_90_out);
  and and_92 (and_92_out, ~ESTADO_00, LINHA_01[0], ~LINHA_01[1], COLUNA_01[0], COLUNA_01[1]);  // AND_Gate
  and and_93 (and_93_out, ESTADO_02, LINHA_02[0], ~LINHA_02[1], COLUNA_02[0], COLUNA_02[1]);  // AND_Gate
  or or_28 (or_28_out, and_93_out, and_92_out);
  and and_94 (and_94_out, ~ESTADO_00, ~LINHA_01[0], LINHA_01[1], COLUNA_01[0], COLUNA_01[1]);  // AND_Gate
  and and_95 (and_95_out, ESTADO_02, ~LINHA_02[0], LINHA_02[1], COLUNA_02[0], COLUNA_02[1]);  // AND_Gate
  or or_29 (or_29_out, and_95_out, and_94_out);
  and and_96 (and_96_out, ~ESTADO_00, LINHA_01[0], LINHA_01[1], COLUNA_01[0], COLUNA_01[1]);  // AND_Gate
  and and_97 (and_97_out, ESTADO_02, LINHA_02[0], LINHA_02[1], COLUNA_02[0], COLUNA_02[1]);
  or or_30 (or_30_out, and_97_out, and_96_out);
  and and_98 (and_98_out, or_27_out, IGUAIS, ESTADO_03, ~RET_P03);  // AND_Gate
  Counter #(.width(1), .max('h1)) counter_19 (
    .Q(RET_P13), .clk(and_99_out), .clr(RESET));  // open: load, D, count, carry
  and and_99 (and_99_out, or_28_out, IGUAIS, ESTADO_03, ~RET_P13);  // AND_Gate
  Counter #(.width(1), .max('h1)) counter_20 (
    .Q(RET_P23), .clk(and_100_out), .clr(RESET));  // open: load, D, count, carry
  and and_100 (and_100_out, or_29_out, IGUAIS, ESTADO_03, ~RET_P23);  // AND_Gate
  Counter #(.width(1), .max('h1)) counter_21 (
    .Q(RET_P33), .clk(and_101_out), .clr(RESET));  // open: load, D, count, carry
  and and_101 (and_101_out, or_30_out, IGUAIS, ESTADO_03, ~RET_P33);  // AND_Gate
  Counter #(.width(1), .max('h1)) counter_22 (
    .Q(RET_P03), .clk(and_98_out), .clr(RESET));  // open: load, D, count, carry
  and and_102 (ACERTO_13, ~RET_P13, or_28_out);  // AND_Gate
  and and_103 (ACERTO_33, ~RET_P33, or_30_out);  // AND_Gate
  or or_31 (or_31_out, and_90_out, and_91_out, RET_P03);
  and and_104 (ACERTO_03, ~RET_P03, or_27_out);  // AND_Gate
  or or_32 (or_32_out, and_92_out, and_93_out, RET_P13);
  Multiplexer #(.width(4)) multiplexer_15 (.in1(4'b0100), .out(P23), .sel(or_33_out));  // open: in0, en
  or or_33 (or_33_out, and_94_out, and_95_out, RET_P23);
  and and_105 (ACERTO_23, ~RET_P23, or_29_out);  // AND_Gate
  Multiplexer #(.width(4)) multiplexer_16 (.in1(4'b0111), .out(P33), .sel(or_34_out));  // open: in0, en
  or or_34 (or_34_out, and_96_out, and_97_out, RET_P33);
  Multiplexer #(.width(4)) multiplexer_17 (.in1(4'b0101), .out(P03), .sel(or_31_out));  // open: in0, en
  Multiplexer #(.width(4)) multiplexer_18 (.in1(4'b0010), .out(P13), .sel(or_32_out));  // open: in0, en

  // Notes on the sheet:
  //   CIRCUITO UTILIZADO PARA MOVIMENTAÇÃO NO TABULEIRO
  //   CIRCUITO QUE DEFINE SE OS NUMEROS SÃO IGUAIS
  //   CIRCUITO RESPONSÁVEL PELA MUDANÇA DE ESTADOS
  //   CIRCUITO DE PONTUAÇÃO DOS JOGADORES
  //   CIRCUITO RESPONSÁVEL POR GUARDAR AS POSIÇÕES
  //   CIRCUITO QUE EVITA QUE UM MESMO ACERTO PONTUA DUAS VEZES
  //   CIRCUITO RESPONSAVEL POR TORNAR OS DISPLAYS VISIVEIS NO TABULEIRO
endmodule
